# Fritzing sketch Layout_GPIO (saved by Fritzing 0.9.3b)
breadboards: 1

parts:
  Raspberry_Pi_1 = Raspberry Pi 3 [part_number=RPI-3-V1.2]  # not connected
  VCC1 = 4 x AAA Battery Mount  # not connected
  RHT1 = Humidity and Temperature Sensor RHT03
  M1 = DC Motor  # not connected
  U1 = Vibration Motor- ROB-08449 [package=vibe-motor-10mm]
  L1 = Inductor [package="1206 [SMD]"]  # not connected
  R1 = Resistor [tolerance=±5% resistance=10 package="0603 [SMD]"]
  IC1 = L293D [package=THT]  # not connected

nets:
  N1: RHT1.Vcc, U1.+
  N2: RHT1.Data-signal, R1.Pin_0
  N3: RHT1.GND_2, U1.-

notes:
  Vibration Sensor
  4.8 V Battery
  Humidity and Temperature Sensor
  10 Ohm
  Current Sensor
